# Fritzing sketch MAX31855K_Breakout (saved by Fritzing 0.9.2b)

parts:
  Part1 = FTDI Basic Programmer
  Part2 = Arduino Pro Mini v13
  PART1 = SparkFun MAX31855K Thermocouple Breakout [part_number=SEN-13266]

nets:
  N1: Part1.DTR, Part2.DTR
  N2: Part1.RXI, Part2.D0/TX
  N3: Part1.TXO, Part2.D1/RX
  N4: Part1.POWER, Part2.VCC
  GND: Part1.CTS, Part1.GND, Part2.GND
  N5: Part2.A1, PART1.GND
  N6: Part2.A0, PART1.VCC
  N7: Part2.D13/SCK, PART1.SCK
  N8: Part2.D12/MISO, PART1.SO
  N9: Part2.D11_PWM/MOSI, PART1.NC
  N10: Part2.D10_PWM/SS, PART1.CS

custom parts:
  SparkFun MAX31855K Thermocouple Breakout: The MAX31855K IC takes a standard k-type thermocouple in one end, digitizes the temperature measured and sends that data out the other end via SPI. For more information, please visit www.sparkfun.com
